# Fritzing sketch arduino (saved by Fritzing 1.0.3b)
breadboards: 1

parts:
  Bauteil1 = Arduino Uno (Rev3)
  R1 = Resistor [tolerance=±5% power=0.25W resistance=220 package=THT]
  DME_Station_Relaiskontakt = TILT-SWITCH-SW-200D [package=reed_switch_plastic]

nets:
  N1: Bauteil1.D7, R1.Pin_1, DME_Station_Relaiskontakt.2
  N2: Bauteil1.5V, DME_Station_Relaiskontakt.1
  N3: Bauteil1.GND, R1.Pin_0
